// Logisim project xetroc.circ as structural Verilog: 12 circuits, main circuit main
module main (
);

  wire arm_control_unit_1_alusrc, arm_control_unit_1_memtoreg, arm_control_unit_1_memwrite,
       arm_control_unit_1_pcsrc, arm_control_unit_1_regwrite, clock_1_out, clock_2_out, reset;
  wire [1:0] arm_control_unit_1_immsrc, arm_control_unit_1_regsrc;
  wire [2:0] arm_control_unit_1_alucontrol, multiplexer_2_out, multiplexer_3_out, multiplexer_4_out;
  wire [2:2] arm_control_unit_1_regsrc_2;
  wire [3:0] alu_1_aluflags;
  wire [15:0] rom_1_data;
  wire [31:0] adder_1_out, adder_2_out, alu_1_result, immediate_1_imm32, multiplexer_1_out,
       multiplexer_5_out, multiplexer_6_out, ram_1_dout, register_1_q, registerfile_1_rd1, registerfile_1_rd2;

  Button u_reset (.out(reset));
  Clock clk ();  // open: out
  Register #(.width(32)) register_1 (
    .D(multiplexer_1_out), .en(1'b1), .clk(clock_1_out), .Q(register_1_q), .clr(reset));
  Multiplexer #(.width(32)) multiplexer_1 (
    .in0(adder_1_out), .in1(multiplexer_6_out), .out(multiplexer_1_out), .sel(arm_control_unit_1_pcsrc));
  Clock clock_1 (.out(clock_1_out));
  ROM #(.addrWidth(16), .dataWidth(16)) rom_1 (.addr(register_1_q[16:1]), .data(rom_1_data));
  // Probe on register_1_q
  Adder #(.width(32)) adder_1 (.a(register_1_q), .b(32'h2), .out(adder_1_out));  // open: cin, cout
  // Probe on arm_control_unit_1_pcsrc
  // Probe on adder_1_out
  // Probe on rom_1_data
  // Probe on arm_control_unit_1_regsrc_2[2]
  Multiplexer #(.width(3)) multiplexer_2 (
    .in0(rom_1_data[5:3]), .in1(rom_1_data[10:8]), .out(multiplexer_2_out),
    .sel(arm_control_unit_1_regsrc_2[2]));
  Multiplexer #(.width(3)) multiplexer_3 (
    .in0(rom_1_data[8:6]), .in1(rom_1_data[10:8]), .out(multiplexer_3_out),
    .sel(arm_control_unit_1_regsrc_2[2]));
  Multiplexer #(.width(3)) multiplexer_4 (
    .in0(rom_1_data[2:0]), .in1(rom_1_data[10:8]), .out(multiplexer_4_out),
    .sel(arm_control_unit_1_regsrc_2[2]));
  Adder #(.width(32)) adder_2 (.a(adder_1_out), .b(32'h2), .out(adder_2_out));  // open: cin, cout
  ARM_Control_Unit arm_control_unit_1 (
    .ALUFlags(alu_1_aluflags), .Instruction(rom_1_data), .PCSrc(arm_control_unit_1_pcsrc),
    .MemToReg(arm_control_unit_1_memtoreg), .MemWrite(arm_control_unit_1_memwrite),
    .ALUControl(arm_control_unit_1_alucontrol), .ALUSrc(arm_control_unit_1_alusrc),
    .ImmSrc(arm_control_unit_1_immsrc), .RegWrite(arm_control_unit_1_regwrite),
    .RegSrc({arm_control_unit_1_regsrc_2[2], arm_control_unit_1_regsrc}));
  // Probe on arm_control_unit_1_regwrite
  // Probe on multiplexer_2_out
  // Probe on multiplexer_3_out
  // Probe on multiplexer_4_out
  // Probe on adder_2_out
  // Probe on arm_control_unit_1_immsrc
  // Probe on arm_control_unit_1_regsrc
  RegisterFile registerfile_1 (
    .SP_PC(arm_control_unit_1_regsrc), .A1(multiplexer_2_out), .A2(multiplexer_3_out),
    .A3(multiplexer_4_out), .WE3(arm_control_unit_1_regwrite), .WD3(multiplexer_6_out), .R15(adder_2_out),
    .RD1(registerfile_1_rd1), .RD2(registerfile_1_rd2));
  Immediate immediate_1 (.op(arm_control_unit_1_immsrc), .inst(rom_1_data), .imm32(immediate_1_imm32));
  // Probe on arm_control_unit_1_alusrc
  Multiplexer #(.width(32)) multiplexer_5 (
    .in0(registerfile_1_rd2), .in1(immediate_1_imm32), .out(multiplexer_5_out),
    .sel(arm_control_unit_1_alusrc));
  // Probe on immediate_1_imm32
  // Probe on arm_control_unit_1_alucontrol
  // Probe on registerfile_1_rd1
  // Probe on multiplexer_5_out
  // Probe on registerfile_1_rd2
  // Probe on alu_1_aluflags
  ALU alu_1 (
    .A(registerfile_1_rd1), .B(multiplexer_5_out), .ALUControl(arm_control_unit_1_alucontrol),
    .Result(alu_1_result), .ALUFlags(alu_1_aluflags));
  // Probe on arm_control_unit_1_memwrite
  RAM #(.addrWidth(16), .asyncread("true"), .dataWidth(32)) ram_1 (
    .addr(alu_1_result[17:2]), .we(arm_control_unit_1_memwrite), .oe(1'b1), .clk(clock_2_out),
    .din(registerfile_1_rd2), .dout(ram_1_dout));
  Clock clock_2 (.out(clock_2_out));
  // Probe on alu_1_result
  // Probe on multiplexer_6_out
  // Probe on arm_control_unit_1_memtoreg
  // Probe on ram_1_dout
  Multiplexer #(.width(32)) multiplexer_6 (
    .in0(alu_1_result), .in1(ram_1_dout), .out(multiplexer_6_out), .sel(arm_control_unit_1_memtoreg));

  // Notes on the sheet:
  //   contents of rom_1 (hex, n*v repeats v):
  //   2156 3203 3b10 c 18d5 1ace 9401 9f01 d0fe e7fe
endmodule

module RegisterFile (
  input  [1:0] SP_PC,
  input  [2:0] A1,
  input  [2:0] A2,
  input  [2:0] A3,
  input  WE3,
  input  [31:0] WD3,
  input  [31:0] R15,
  output [31:0] RD1,
  output [31:0] RD2
);

  wire clock_1_out, decoder_1_out0, decoder_1_out1, decoder_1_out2, decoder_1_out3, decoder_1_out4,
       decoder_1_out5, decoder_1_out6, decoder_1_out7;
  wire [3:0] multiplexer_1_out;
  wire [31:0] R0_q, R1_q, R2_q, R3_q, R4_q, R5_q, R6_q, R7_q;

  Clock clock_1 (.out(clock_1_out));
  // Probe on A3
  Decoder #(.select(3)) decoder_1 (
    .out0(decoder_1_out0), .out1(decoder_1_out1), .out2(decoder_1_out2), .out3(decoder_1_out3),
    .out4(decoder_1_out4), .out5(decoder_1_out5), .out6(decoder_1_out6), .out7(decoder_1_out7), .sel(A3),
    .en(WE3));
  Multiplexer #(.select(2), .width(4)) multiplexer_1 (
    .in0({1'b0, A1}), .in1(4'b1111), .in2(4'b1110), .out(multiplexer_1_out), .sel(SP_PC));  // open: in3
  Register #(.width(32)) R0 (.D(WD3), .en(decoder_1_out0), .clk(clock_1_out), .Q(R0_q));  // open: clr
  Register #(.width(32)) R1 (.D(WD3), .en(decoder_1_out1), .clk(clock_1_out), .Q(R1_q));  // open: clr
  Register #(.width(32)) R2 (.D(WD3), .en(decoder_1_out2), .clk(clock_1_out), .Q(R2_q));  // open: clr
  Register #(.width(32)) R3 (.D(WD3), .en(decoder_1_out3), .clk(clock_1_out), .Q(R3_q));  // open: clr
  Register #(.width(32)) R4 (.D(WD3), .en(decoder_1_out4), .clk(clock_1_out), .Q(R4_q));  // open: clr
  Register #(.width(32)) R5 (.D(WD3), .en(decoder_1_out5), .clk(clock_1_out), .Q(R5_q));  // open: clr
  Register #(.width(32)) R6 (.D(WD3), .en(decoder_1_out6), .clk(clock_1_out), .Q(R6_q));  // open: clr
  Register #(.width(32)) R7 (.D(WD3), .en(decoder_1_out7), .clk(clock_1_out), .Q(R7_q));  // open: clr
  // Probe on A2
  Multiplexer #(.select(3), .width(32)) multiplexer_2 (
    .in0(R0_q), .in1(R1_q), .in2(R2_q), .in3(R3_q), .in4(R4_q), .in5(R5_q), .in6(R6_q), .in7(R7_q),
    .out(RD2), .sel(A2));
  // Probe on multiplexer_1_out
  Multiplexer #(.select(4), .width(32)) multiplexer_3 (
    .in0(R0_q), .in1(R1_q), .in2(R2_q), .in3(R3_q), .in4(R4_q), .in5(R5_q), .in6(R6_q), .in7(R7_q),
    .in14({32{1'b0}}), .in15(R15), .out(RD1), .sel(multiplexer_1_out));  // open: in8, in9, in10, in11, in12, in13

  // Notes on the sheet:
  //   PC
  //   SP
  //   SP is fixed to 0
  //   SP
  //   PC
endmodule

module ALU (
  input  [2:0] ALUControl,
  input  [31:0] A,
  input  [31:0] B,
  output [31:0] Result,
  output [3:0] ALUFlags
);

  wire Adder_carryout, not_2_out, Sum31, xnor_1_out, xor_1_out;
  wire [30:0] Adder_sum;
  wire [31:0] and_1_out, multiplexer_1_out, multiplexer_2_out, not_1_out, or_1_out;

  Multiplexer #(.width(32)) multiplexer_1 (.in0({32{1'b0}}), .in1(A), .out(multiplexer_1_out), .sel(ALUControl[2]));
  assign not_1_out = ~B;  // NOT_Gate not_1, 32 bits wide
  Multiplexer #(.width(32)) multiplexer_2 (.in0(B), .in1(not_1_out), .out(multiplexer_2_out), .sel(ALUControl[0]));
  assign and_1_out = B & multiplexer_1_out;  // AND_Gate and_1, 32 bits wide
  assign or_1_out = B | multiplexer_1_out;  // OR_Gate or_1, 32 bits wide
  xor xor_1 (xor_1_out, Sum31, multiplexer_1_out[31]);
  NotExactlyOne xnor_1 (.out(xnor_1_out), .in0(multiplexer_1_out[31]), .in1(B[31]), .in2(ALUControl[0]));
  Adder_32_bit Adder (
    .A(multiplexer_1_out), .B(multiplexer_2_out), .CarryIn(ALUControl[0]), .CarryOut(Adder_carryout),
    .Sum({Sum31, Adder_sum}));
  not not_2 (not_2_out, ALUControl[1]);
  Multiplexer #(.select(3), .width(32)) multiplexer_3 (
    .in0({Sum31, Adder_sum}), .in1({Sum31, Adder_sum}), .in2({32{1'b0}}), .in3(A), .in4({Sum31, Adder_sum}),
    .in5({Sum31, Adder_sum}), .in6(and_1_out), .in7(or_1_out), .out({ALUFlags[3], Result[30:0]}),
    .sel(ALUControl));
  and and_2 (ALUFlags[1], Adder_carryout, not_2_out);
  and and_3 (ALUFlags[0], not_2_out, xor_1_out, xnor_1_out);
  Zero_Detect_32_bit Zero_Detect (.A({ALUFlags[3], Result[30:0]}), .B(ALUFlags[2]));

  assign Result[31] = ALUFlags[3];

  // Notes on the sheet:
  //   000 B
  //   001 -B
  //   010 0
  //   011 A
  //   100 A + B
  //   101 A - B
  //   110 A & B
  //   111 A | B
  //   Negative
  //   Carry
  //   oVerflow
  //   Zero
  //   NZCV
endmodule

module Immediate (
  input  [1:0] op,
  input  [15:0] inst,
  output [31:0] imm32
);

  wire [29:0] bit_extender_2_out;
  wire [30:0] bit_extender_3_out, bit_extender_4_out;
  wire [31:0] bit_extender_1_out;

  assign bit_extender_1_out = {{24{1'b0}}, inst[7:0]};  // Bit_Extender bit_extender_1
  assign bit_extender_2_out = {{22{1'b0}}, inst[7:0]};  // Bit_Extender bit_extender_2
  assign bit_extender_3_out = {{23{inst[7]}}, inst[7:0]};  // Bit_Extender bit_extender_3
  assign bit_extender_4_out = {{20{inst[10]}}, inst[10:0]};  // Bit_Extender bit_extender_4
  Multiplexer #(.select(2), .width(32)) multiplexer_1 (
    .in0(bit_extender_1_out), .in1({bit_extender_2_out, 2'b00}), .in2({bit_extender_3_out, 1'b0}),
    .in3({bit_extender_4_out, 1'b0}), .out(imm32), .sel(op));

  // Notes on the sheet:
  //   00: imm8
  //   01: imm8 << 2
  //   10: simm8 << 1
  //   11: simm11 << 1
endmodule

module ARM_Condition_Check (
  input  [3:0] Cond,
  input  [3:0] ALUFlags,
  output CondEx
);

  wire and_1_out, and_2_out, not_1_out, not_2_out, not_3_out, not_4_out, not_5_out, not_6_out, not_7_out,
       xor_1_out;

  xor xor_1 (xor_1_out, ALUFlags[3], ALUFlags[0]);
  and and_1 (and_1_out, ~ALUFlags[2], ALUFlags[1]);  // AND_Gate
  not not_1 (not_1_out, xor_1_out);
  and and_2 (and_2_out, not_1_out, ~ALUFlags[2]);  // AND_Gate
  not not_2 (not_2_out, ALUFlags[2]);
  not not_3 (not_3_out, ALUFlags[1]);
  not not_4 (not_4_out, ALUFlags[3]);
  not not_5 (not_5_out, ALUFlags[0]);
  not not_6 (not_6_out, and_1_out);
  not not_7 (not_7_out, and_2_out);
  Multiplexer #(.select(4)) multiplexer_1 (
    .in0(ALUFlags[2]), .in1(not_2_out), .in2(ALUFlags[1]), .in3(not_3_out), .in4(ALUFlags[3]),
    .in5(not_4_out), .in6(ALUFlags[0]), .in7(not_5_out), .in8(and_1_out), .in9(not_6_out), .in10(not_1_out),
    .in11(xor_1_out), .in12(and_2_out), .in13(not_7_out), .in14(1'b1), .out(CondEx), .sel(Cond));  // open: in15

  // Other names for the same wires on the sheet: V = ALUFlags[0]; C = ALUFlags[1]; Z = ALUFlags[2]; N = ALUFlags[3]

  // Notes on the sheet:
  //   Negative
  //   Zero
  //   Carry
  //   oVerflow
endmodule

module ARM_Conditional_Logic (
  input  [3:0] ALUFlags,
  input  [1:0] FlagW,
  input  [3:0] Cond,
  input  MemW,
  input  NoWrite,
  input  RegW,
  input  PCS,
  output PCSrc,
  output RegWrite,
  output MemWrite
);

  wire and_1_out, and_2_out, arm_condition_check_1_condex, clock_1_out;
  wire [1:0] ALUFlags_01_q, ALUFlags_32_q;

  Clock clock_1 (.out(clock_1_out));
  and and_1 (and_1_out, FlagW[1], arm_condition_check_1_condex);
  and and_2 (and_2_out, FlagW[0], arm_condition_check_1_condex);
  Register #(.width(2)) ALUFlags_32 (
    .D(ALUFlags[3:2]), .en(and_1_out), .clk(clock_1_out), .Q(ALUFlags_32_q));  // open: clr
  Register #(.width(2)) ALUFlags_01 (
    .D(ALUFlags[1:0]), .en(and_2_out), .clk(clock_1_out), .Q(ALUFlags_01_q));  // open: clr
  ARM_Condition_Check arm_condition_check_1 (
    .Cond(Cond), .ALUFlags({ALUFlags_32_q, ALUFlags_01_q}), .CondEx(arm_condition_check_1_condex));
  and and_3 (PCSrc, PCS, arm_condition_check_1_condex);
  and and_4 (RegWrite, RegW, ~NoWrite, arm_condition_check_1_condex);  // AND_Gate
  and and_5 (MemWrite, MemW, arm_condition_check_1_condex);

  // Other names for the same wires on the sheet: ALUFlags01[1:0] = ALUFlags[1:0]; ALUFlags32[1:0] = ALUFlags[3:2]
endmodule

module ARM_Decoder (
  input  [6:0] Opcode,
  output \always ,
  output PCS,
  output MemToReg,
  output MemW,
  output ALUSrc,
  output [1:0] ImmSrc,
  output RegW,
  output [2:0] RegSrc,
  output [2:0] ALUControl,
  output [1:0] FlagW
);

  wire and_3_out, and_4_out, and_5_out, and_6_out, and_7_out, and_10_out, and_11_out, and_12_out, not_2_out,
       not_3_out, not_4_out, not_5_out;

  not not_1 (FlagW[0], Opcode[6]);
  not not_2 (not_2_out, Opcode[5]);
  not not_3 (not_3_out, Opcode[4]);
  not not_4 (not_4_out, Opcode[3]);
  not not_5 (not_5_out, Opcode[2]);
  or or_1 (\always , not_2_out, not_4_out);
  and and_1 (MemToReg, Opcode[6], not_2_out, Opcode[2]);
  and and_2 (MemW, Opcode[6], not_2_out, not_5_out);
  or or_2 (ALUSrc, Opcode[6], Opcode[4]);
  and and_3 (and_3_out, Opcode[6], not_4_out);
  and and_4 (and_4_out, not_2_out, not_3_out);
  and and_5 (and_5_out, not_2_out, not_5_out);
  and and_6 (and_6_out, Opcode[6], not_2_out);
  and and_7 (and_7_out, not_2_out, Opcode[4]);
  and and_8 (RegSrc[1], Opcode[6], not_2_out);
  or or_3 (ALUControl[2], Opcode[3], Opcode[6]);
  and and_9 (ALUControl[1], not_3_out, not_4_out);
  and and_10 (and_10_out, Opcode[4], Opcode[2]);
  and and_11 (and_11_out, not_3_out, not_4_out);
  and and_12 (and_12_out, FlagW[0], not_3_out, Opcode[0]);
  and and_13 (FlagW[1], FlagW[0], Opcode[3]);
  or or_4 (ImmSrc[0], and_3_out, and_4_out);
  or or_5 (RegW, and_5_out, FlagW[0]);
  or or_6 (RegSrc[2], and_6_out, and_7_out);
  or or_7 (ALUControl[0], and_10_out, and_11_out, and_12_out);

  assign ImmSrc[1] = Opcode[5];
  assign PCS = Opcode[5];
  assign RegSrc[0] = Opcode[5];
endmodule

module ARM_Control_Unit (
  input  [3:0] ALUFlags,
  input  [15:0] Instruction,
  output PCSrc,
  output MemToReg,
  output MemWrite,
  output [2:0] ALUControl,
  output ALUSrc,
  output [1:0] ImmSrc,
  output RegWrite,
  output [2:0] RegSrc
);

  wire arm_decoder_1_always, arm_decoder_1_memw, arm_decoder_1_pcs, arm_decoder_1_regw, undriven;
  wire [1:0] arm_decoder_1_flagw;
  wire [3:0] multiplexer_1_out;

  Multiplexer #(.width(4)) multiplexer_1 (
    .in0(Instruction[11:8]), .in1(4'b1110), .out(multiplexer_1_out), .sel(arm_decoder_1_always));
  ARM_Decoder arm_decoder_1 (
    .Opcode(Instruction[15:9]), .\always (arm_decoder_1_always), .PCS(arm_decoder_1_pcs),
    .MemToReg(MemToReg), .MemW(arm_decoder_1_memw), .ALUSrc(ALUSrc), .ImmSrc(ImmSrc),
    .RegW(arm_decoder_1_regw), .RegSrc(RegSrc), .ALUControl(ALUControl), .FlagW(arm_decoder_1_flagw));
  ARM_Conditional_Logic arm_conditional_logic_1 (
    .ALUFlags(ALUFlags), .FlagW(arm_decoder_1_flagw), .Cond(multiplexer_1_out), .MemW(arm_decoder_1_memw),
    .NoWrite(undriven), .RegW(arm_decoder_1_regw), .PCS(arm_decoder_1_pcs), .PCSrc(PCSrc),
    .RegWrite(RegWrite), .MemWrite(MemWrite));

  // Notes on the sheet:
  //   always
  //   1 for writing WriteData to RAM 
  //   ALU operation
  //   1 for using computed Result for PC
  //   1 for using RAM ReadData, else ALUResult
  //   0 for using RD2 1 for ExtImm as ALU SrcB
  //   select which kind of imm exension to ExtImm
  //   1 for RegisterFile write enable (WE3)
  //   select which instruction bits are used for RA2
endmodule

module Adder_1_bit (
  input  CarryIn,
  input  a,
  input  b,
  output CarryOut,
  output Sum
);

  wire and_1_out, and_2_out, and_3_out, and_4_out, and_5_out, and_6_out, and_7_out;

  and and_1 (and_1_out, CarryIn, a);
  and and_2 (and_2_out, CarryIn, b);
  and and_3 (and_3_out, a, b);
  and and_4 (and_4_out, a, ~b, ~CarryIn);  // AND_Gate
  and and_5 (and_5_out, ~a, b, ~CarryIn);  // AND_Gate
  and and_6 (and_6_out, ~a, ~b, CarryIn);  // AND_Gate
  and and_7 (and_7_out, a, b, CarryIn);
  or or_1 (CarryOut, and_1_out, and_2_out, and_3_out);
  or or_2 (Sum, and_4_out, and_5_out, and_6_out, and_7_out);
endmodule

module Adder_32_bit (
  input  CarryIn,
  input  [31:0] A,
  input  [31:0] B,
  output [31:0] Sum,
  output CarryOut
);

  Adder #(.width(32)) adder_1 (.a(A), .b(B), .out(Sum), .cin(CarryIn), .cout(CarryOut));
endmodule

module Zero_Detect_32_bit (
  input  [31:0] A,
  output B
);

  nor nor_1 (B, A[0], A[1], A[2], A[3], A[4], A[5], A[6], A[7], A[8], A[9], A[10], A[11], A[12], A[13], A[14], A[15], A[16], A[17], A[18], A[19], A[20], A[21], A[22], A[23], A[24], A[25], A[26], A[27], A[28], A[29], A[30], A[31]);
endmodule

module RegisterSelect (
  input  [2:0] RegSel,
  input  [15:0] instr,
  output [3:0] RA1,
  output [3:0] RA2,
  output [3:0] RA3
);

  wire [2:0] multiplexer_1_out, multiplexer_2_out, multiplexer_3_out;

  Multiplexer #(.width(3)) multiplexer_1 (
    .in0(instr[8:6]), .in1(instr[10:8]), .out(multiplexer_1_out), .sel(RegSel[2]));
  Multiplexer #(.width(3)) multiplexer_2 (.in0(instr[2:0]), .in1(instr[5:3]), .out(multiplexer_2_out), .sel(RegSel[0]));
  Multiplexer #(.width(3)) multiplexer_3 (
    .in0(instr[5:3]), .in1(instr[10:8]), .out(multiplexer_3_out), .sel(RegSel[1]));
  assign RA1 = {{1{1'b0}}, multiplexer_2_out};  // Bit_Extender bit_extender_1
  assign RA2 = {{1{1'b0}}, multiplexer_3_out};  // Bit_Extender bit_extender_2
  assign RA3 = {{1{1'b0}}, multiplexer_1_out};  // Bit_Extender bit_extender_3

  // Notes on the sheet:
  //   000 is like in ADDS <Rd>,<Rn>,<Rm>
  //   Rm
  //   Rn
  //   Rd
endmodule
